# Fritzing sketch schematic (saved by Fritzing 0.7.1b)
breadboards: 1

parts:
  Netduino = Arduino
  J1 = Infrared Proximity Sensor
  J2 = Infrared Proximity Sensor
  Part1 = Arduino Musical Instrument Shield
  Part2 = IMU Analog Combo Board - 5 Degrees of Freedom
  Pololu_Dual_Motor_Driver1 = Pololu_Dual_VNH2SP30_Motor_Driver_Carrier_MD03A

nets:
  GND: Netduino.GND, J1.GND, J2.GND
  N1: Netduino.D13, Pololu_Dual_Motor_Driver1.1_INA
  N2: Netduino.D12, Pololu_Dual_Motor_Driver1.1_INB
  N3: Netduino.D11, Pololu_Dual_Motor_Driver1.1_PWM
  N4: Netduino.D10, Pololu_Dual_Motor_Driver1.2_PWM
  N5: Netduino.D8, Pololu_Dual_Motor_Driver1.2_INB
  N6: Netduino.D7, Pololu_Dual_Motor_Driver1.2_INA
  N7: Netduino.D4, Part1.MIDI-RESET
  N8: Netduino.D3, Part1.MIDI-IN
  VCC: Netduino.+5V, J1.Vcc, J2.Vcc
  N9: Netduino.A0, J2.Vout
  N10: Netduino.A1, J1.Vout
  N11: Netduino.A2, Pololu_Dual_Motor_Driver1.1_CS
  N12: Netduino.A3, Pololu_Dual_Motor_Driver1.2_CS
  N13: Netduino.A4, Part2.YRATE
  N14: Netduino.A5, Part2.XRATE

notes:
  WiFi Chip Here. Gets full U1RX/TX
  Receive bytes from Remote (RF). Only uses U2RX on Netduino
